# Fritzing sketch Dashboard PIR Test (saved by Fritzing 0.9.3b)
breadboards: 1

parts:
  R1 = Resistor [tolerance=±5% resistance=470 package=THT]
  LED1 = LED - 5mm [color="Red (633nm)" package="5 mm [THT]"]  # not connected
  PIR1 = PIR sensor
  Raspberry_Pi2 = Raspberry Pi 2

nets:
  N1: R1.Pin_0, Raspberry_Pi2.GPIO18
  VDD: PIR1.VDD, Raspberry_Pi2.5V
  N2: PIR1.SIG, Raspberry_Pi2.GPIO23
  GND: PIR1.GND, Raspberry_Pi2.GND
